// Logisim project Adders.circ as structural Verilog: 1 circuit, main circuit main
module main (
);

  wire and_1_out, and_2_out, and_3_out, and_4_out, and_5_out, and_6_out, and_7_out, nand_1_out, nand_2_out,
       nand_3_out, nand_4_out, nand_5_out, nand_6_out, nand_7_out, nand_8_out, nand_9_out, nand_10_out,
       nand_11_out, nand_12_out, nand_13_out, nand_14_out, or_1_out, or_2_out, or_3_out, xor_1_out,
       xor_2_out, xor_3_out, xor_4_out, xor_5_out, xor_6_out, xor_7_out;

  nand nand_1 (nand_1_out, 1'b1, 1'b1);
  nand nand_2 (nand_2_out, 1'b1, 1'b1);
  nand nand_3 (nand_3_out, 1'b1, nand_1_out);
  nand nand_4 (nand_4_out, nand_1_out, 1'b1);
  nand nand_5 (nand_5_out, 1'b1, nand_2_out);
  nand nand_6 (nand_6_out, nand_2_out, 1'b1);
  xor xor_1 (xor_1_out, 1'b1, 1'b1);
  and and_1 (and_1_out, 1'b1, 1'b1);
  xor xor_2 (xor_2_out, 1'b1, 1'b1);
  and and_2 (and_2_out, 1'b1, 1'b1);
  xor xor_3 (xor_3_out, 1'b1, 1'b1);
  and and_3 (and_3_out, 1'b1, 1'b1);
  xor xor_4 (xor_4_out, 1'b1, 1'b1);
  and and_4 (and_4_out, 1'b1, 1'b1);
  nand nand_7 (nand_7_out, nand_3_out, nand_4_out);
  LED led_1 (.in(nand_7_out));
  nand nand_8 (nand_8_out, nand_5_out, nand_6_out);
  LED led_2 (.in(xor_1_out));
  xor xor_5 (xor_5_out, xor_2_out, and_1_out);
  xor xor_6 (xor_6_out, xor_3_out, or_1_out);
  xor xor_7 (xor_7_out, xor_4_out, or_2_out);
  nand nand_9 (nand_9_out, nand_1_out, nand_1_out);
  LED led_3 (.in(nand_9_out));
  LED led_4 (.in(xor_5_out));
  and and_5 (and_5_out, and_1_out, xor_2_out);
  LED led_5 (.in(xor_6_out));
  and and_6 (and_6_out, or_1_out, xor_3_out);
  LED led_6 (.in(xor_7_out));
  and and_7 (and_7_out, or_2_out, xor_4_out);
  nand nand_10 (nand_10_out, nand_8_out, 1'b1);
  or or_1 (or_1_out, and_5_out, and_2_out);
  or or_2 (or_2_out, and_6_out, and_3_out);
  or or_3 (or_3_out, and_7_out, and_4_out);
  nand nand_11 (nand_11_out, nand_8_out, nand_10_out);
  nand nand_12 (nand_12_out, nand_10_out, 1'b1);
  LED led_7 (.in(or_3_out));
  nand nand_13 (nand_13_out, nand_11_out, nand_12_out);
  nand nand_14 (nand_14_out, nand_10_out, nand_2_out);
  LED led_8 (.in(nand_14_out));
  LED led_9 (.in(nand_13_out));

  // Notes on the sheet:
  //   Half Adder
  //   Full Adder
  //   4-bit adder
endmodule
