// Logisim project Mux_Encoder.circ as structural Verilog: 1 circuit, main circuit main
module main (
);

  wire and_1_out, and_2_out, and_3_out, and_4_out, and_5_out, and_6_out, and_7_out, and_8_out,
       dipswitch_1_p1, dipswitch_1_p2, dipswitch_1_p3, dipswitch_2_p1, dipswitch_2_p2, dipswitch_2_p3,
       dipswitch_2_p4, dipswitch_2_p5, dipswitch_2_p6, dipswitch_2_p7, not_1_out, not_2_out, not_3_out,
       or_1_out, or_2_out, or_3_out, or_4_out;

  // DipSwitch #(.number(3)) dipswitch_1: pin names not known; wires that end beside it: dipswitch_1_p1, dipswitch_1_p2, dipswitch_1_p3
  // DipSwitch #(.number(7)) dipswitch_2: pin names not known; wires that end beside it: dipswitch_2_p1, dipswitch_2_p2, dipswitch_2_p3, dipswitch_2_p4, dipswitch_2_p5, dipswitch_2_p6, dipswitch_2_p7
  not not_1 (not_1_out, dipswitch_1_p2);
  not not_2 (not_2_out, dipswitch_1_p3);
  not not_3 (not_3_out, dipswitch_1_p1);
  and and_1 (and_1_out, not_3_out, not_1_out, not_2_out, 1'b1);
  and and_2 (and_2_out, dipswitch_1_p1, not_1_out, not_2_out, 1'b1);
  and and_3 (and_3_out, not_3_out, dipswitch_1_p2, not_2_out, 1'b1);
  and and_4 (and_4_out, dipswitch_1_p1, dipswitch_1_p2, not_2_out, 1'b1);
  and and_5 (and_5_out, not_3_out, not_1_out, dipswitch_1_p3, 1'b1);
  and and_6 (and_6_out, dipswitch_1_p1, not_1_out, dipswitch_1_p3, 1'b1);
  and and_7 (and_7_out, not_3_out, dipswitch_1_p2, dipswitch_1_p3, 1'b1);
  and and_8 (and_8_out, dipswitch_1_p1, dipswitch_1_p2, dipswitch_1_p3, 1'b1);
  or or_1 (or_1_out, dipswitch_2_p1, dipswitch_2_p3, dipswitch_2_p5, dipswitch_2_p7);
  or or_2 (or_2_out, dipswitch_2_p2, dipswitch_2_p3, dipswitch_2_p6, dipswitch_2_p7);
  or or_3 (or_3_out, dipswitch_2_p4, dipswitch_2_p5, dipswitch_2_p6, dipswitch_2_p7);
  LED led_1 (.in(or_1_out));
  LED led_2 (.in(or_2_out));
  LED led_3 (.in(or_3_out));
  LedBar ledbar_1 (
    .led0(and_1_out), .led1(and_2_out), .led2(and_3_out), .led3(and_4_out), .led4(and_5_out),
    .led5(and_6_out), .led6(and_7_out), .led7(and_8_out));
  or or_4 (or_4_out, and_1_out, and_2_out, and_3_out, and_4_out, and_5_out, and_6_out, and_7_out, and_8_out);
  LED led_4 (.in(or_4_out));

  // Notes on the sheet:
  //   S2
  //   S1
  //   8x3 Encoder
  //   S0
  //   i0
  //   i1
  //   i2
  //   i3
  //   i4
  //   i5
  //   i6
  //   i7
  //   A0
  //   A1
  //   A2
  //   8x1 Mux
endmodule
